# Fritzing sketch romi (saved by Fritzing 0.9.6b)
circuit board: 9.05228cm x 5.7785cm
breadboards: 1

parts:
  PIC_left = PIC16F1705 [part_number=PIC16F1705 package="DIP (Dual Inline) [THT]"]
  PIC_right = PIC16F1705 [part_number=PIC16F1705 package="DIP (Dual Inline) [THT]"]
  SDA = Resistor [tolerance=±5% resistance=10000 power=0.25 package=THT]
  MCLR = Resistor [tolerance=±5% resistance=10000 power=0.25 package=THT]
  led_left = Resistor [tolerance=±5% resistance=1k power=0.25 package=THT]
  led_right = Resistor [tolerance=±5% resistance=1k power=0.25 package=THT]
  LED_left = LED - 3mm [color="Red (633nm)" current=0.030 package="3 mm [THT]"]
  LED_right = LED - 3mm [color="Red (633nm)" current=0.030 package="3 mm [THT]"]
  PWR_5v = Screw terminal - 2 pins [package=THT]
  SCL = Resistor [tolerance=±5% resistance=10000 power=0.25 package=THT]
  RST = SWITCH-MOMENTARY-2 [package=tactile-pth]
  RST/I2C = Camdenboss CTB0158-3 [part_number=CTB0158-3 package=THT]
  PICKIT_left = Header 5 [package=molex-1x5-ra]
  MOTOR_left = Header 5 [package=molex-1x5-ra]
  MOTOR_right = Header 5 [package=molex-1x5-ra]
  PICKIT_right = Header 5 [package=molex-1x5-ra]

nets:
  VDD: PIC_left.Vdd, PIC_right.Vdd, PIC_right.RC4, SDA.Pin_0, PWR_5v.pin1, SCL.Pin_0, PICKIT_left.2, PICKIT_right.2
  N1: PIC_left.RA5, MOTOR_left.1
  N2: PIC_left.RA4, MOTOR_left.2
  N3: PIC_left.MCLR/RA3, PIC_right.MCLR/RA3, MCLR.Pin_1, RST.2, PICKIT_left.1, PICKIT_right.1
  N4: PIC_left.RC5, MOTOR_left.3
  N5: PIC_left.RC4, PIC_left.RC2, PIC_right.RC2, led_left.Pin_0, led_right.Pin_0, PWR_5v.pin2, RST.1, PICKIT_left.3, PICKIT_right.3
  N6: PIC_left.RC3, LED_left.anode
  VSS: PIC_left.Vss, PIC_right.Vss, SCL.Pin_1, RST/I2C.pin2
  N7: PIC_left.RA0, PIC_right.RA0, SDA.Pin_1, RST/I2C.pin3
  N8: PIC_left.RA1, MOTOR_left.5
  N9: PIC_left.RA2, MOTOR_left.4
  N10: PIC_left.RC0, PICKIT_left.5
  N11: PIC_left.RC1, PICKIT_left.4
  N12: PIC_right.RA5, MOTOR_right.1
  N13: PIC_right.RA4, MOTOR_right.2
  N14: PIC_right.RC5, MOTOR_right.3
  N15: PIC_right.RC3, LED_right.anode
  N16: PIC_right.RA1, MOTOR_right.5
  N17: PIC_right.RA2, MOTOR_right.4
  N18: PIC_right.RC0, PICKIT_right.5
  N19: PIC_right.RC1, PICKIT_right.4
  N20: MCLR.Pin_0, RST/I2C.pin1
  N21: led_left.Pin_1, LED_left.cathode
  N22: led_right.Pin_1, LED_right.cathode

custom parts:
  PIC16F1705: Microchip PIC16F1705
  Header 5: Header 6 Standard 6-pin 0.1 header. Use with straight break away headers (SKU : PRT-00116), right angle break away headers (PRT-00553), swiss pins (PRT-00743), machine pins (PRT-00117), and female headers (PRT-00115). Molex polarized connector foot print use with SKU : PRT-08094 with associated crimp pins and housings. NOTES ON THE VARIANTS LOCK and LOCK_LONGPADS... This footprint was designed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
